// Logisim project gates_曾舒立PB19000200.circ as structural Verilog: 6 circuits, main circuit and
module \and  (
  input  in_1,
  input  in_2,
  output out_3
);

  wire transistor_2_out;

  Transistor transistor_1 (.in(1'b0), .out(out_3), .gate(in_2));
  Transistor #(.\type ("n")) transistor_2 (.in(1'b1), .out(transistor_2_out), .gate(in_1));
  Transistor #(.\type ("n")) transistor_3 (.in(transistor_2_out), .out(out_3), .gate(in_2));
  Transistor transistor_4 (.in(1'b0), .out(out_3), .gate(in_1));

  // Notes on the sheet:
  //   曾舒立PB19000200
  //   与门
endmodule

module mux121 (
  input  in_1,
  input  in_2,
  input  in_3,
  output out_4
);

  wire and_1_out_3, and_2_out_3, not_1_out_2;

  \and  and_1 (.in_2(in_1), .out_3(and_1_out_3), .in_1(in_3));
  \not  not_1 (.in_1(in_3), .out_2(not_1_out_2));
  \and  and_2 (.in_2(in_2), .out_3(and_2_out_3), .in_1(not_1_out_2));
  \or  or_1 (.in_1(and_1_out_3), .in_2(and_2_out_3), .out_3(out_4));

  // Notes on the sheet:
  //   曾舒立PB19000200
endmodule

module \or  (
  input  in_1,
  input  in_2,
  output out_3
);

  wire transistor_4_out;

  Transistor #(.\type ("n")) transistor_1 (.in(1'b1), .out(out_3), .gate(in_1));
  Transistor #(.\type ("n")) transistor_2 (.in(1'b1), .out(out_3), .gate(in_2));
  Transistor transistor_3 (.in(transistor_4_out), .out(out_3), .gate(in_2));
  Transistor transistor_4 (.in(1'b0), .out(transistor_4_out), .gate(in_1));

  // Notes on the sheet:
  //   或门
  //   曾舒立PB19000200
endmodule

module \not  (
  input  in_1,
  output out_2
);

  Transistor transistor_1 (.in(1'b1), .out(out_2), .gate(in_1));
  Transistor #(.\type ("n")) transistor_2 (.in(1'b0), .out(out_2), .gate(in_1));

  // Notes on the sheet:
  //   非门
  //   曾舒立PB19000200
endmodule

module mux221 (
  input  in_1,
  input  in_2,
  input  in_3,
  input  in_4,
  input  in_5,
  output out_6,
  output out_7
);

  mux121 mux121_1 (.in_1(in_1), .in_2(in_3), .in_3(in_5), .out_4(out_6));
  mux121 mux121_2 (.in_1(in_2), .in_2(in_4), .in_3(in_5), .out_4(out_7));

  // Notes on the sheet:
  //   曾舒立PB19000200
endmodule

module mux241 (
  input  [1:0] in_1,
  input  [1:0] in_2,
  input  [1:0] in_3,
  input  [1:0] in_4,
  input  [1:0] in_5,
  output [1:0] out_6
);

  wire mux221_1_out_6, mux221_1_out_7, mux221_2_out_6, mux221_2_out_7, not_1_out_2, not_2_out_2;

  \not  not_1 (.in_1(in_5[1]), .out_2(not_1_out_2));
  \not  not_2 (.in_1(in_5[0]), .out_2(not_2_out_2));
  mux221 mux221_1 (
    .in_1(in_1[0]), .in_2(in_1[1]), .in_3(in_2[0]), .in_4(in_2[1]), .in_5(not_2_out_2),
    .out_6(mux221_1_out_6), .out_7(mux221_1_out_7));
  mux221 mux221_2 (
    .in_1(in_3[0]), .in_2(in_3[1]), .in_3(in_4[0]), .in_4(in_4[1]), .in_5(not_2_out_2),
    .out_6(mux221_2_out_6), .out_7(mux221_2_out_7));
  mux221 mux221_3 (
    .in_1(mux221_1_out_6), .in_2(mux221_1_out_7), .in_3(mux221_2_out_6), .in_4(mux221_2_out_7),
    .in_5(not_1_out_2), .out_6(out_6[0]), .out_7(out_6[1]));

  // Notes on the sheet:
  //   曾舒立PB19000200
endmodule
