// Logisim project 名字_曾舒立PB19000200.circ as structural Verilog: 1 circuit, main circuit main
module main (
);

  DotMatrix #(.inputtype("row"), .matrixcols(16), .matrixrows(16)) dotmatrix_1 (
    .row0(16'h1010), .row1(16'h820), .row2(16'h440), .row3(16'h1ff8), .row4(16'h1088), .row5(16'h12a8),
    .row6(16'h11c8), .row7(16'h1ff8), .row8({16{1'b0}}), .row9(16'h3e0), .row10(16'h220), .row11(16'h220),
    .row12(16'h3e0), .row13(16'h220), .row14(16'h220), .row15(16'h3e0));
  DotMatrix #(.inputtype("row"), .matrixcols(16), .matrixrows(16)) dotmatrix_2 (
    .row0(16'h800), .row1(16'h1400), .row2(16'h227c), .row3(16'h5d08), .row4(16'h830), .row5(16'h810),
    .row6(16'h1cfe), .row7(16'h814), .row8(16'h810), .row9(16'h3e10), .row10(16'h10), .row11(16'h3e10),
    .row12(16'h2250), .row13(16'h2230), .row14(16'h2210), .row15(16'h3e00));
  DotMatrix #(.inputtype("row"), .matrixcols(16), .matrixrows(16)) dotmatrix_3 (
    .row0({16{1'b0}}), .row1(16'h400), .row2(16'h200), .row3(16'h100), .row4(16'h80), .row5(16'h1ff8),
    .row6({16{1'b0}}), .row7(16'h810), .row8(16'h420), .row9(16'h240), .row10(16'h180), .row11({16{1'b0}}),
    .row12(16'h3ffc), .row13({16{1'b0}}), .row14({16{1'b0}}), .row15({16{1'b0}}));

  // Notes on the sheet:
  //   PB19000200 曾舒立
endmodule
