// Logisim project 学号_曾舒立PB19000200 .circ as structural Verilog: 1 circuit, main circuit main
module main (
);

  _7_Segment_Display u_7_segment_display_1 (
    .g(1'b1), .f(1'b1), .a(1'b1), .b(1'b1), .e(1'b1), .d(1'b0), .c(1'b0), .dp(1'b0));
  _7_Segment_Display u_7_segment_display_2 (
    .g(1'b1), .f(1'b1), .a(1'b0), .b(1'b0), .e(1'b1), .d(1'b1), .c(1'b1), .dp(1'b0));
  _7_Segment_Display u_7_segment_display_3 (
    .g(1'b0), .f(1'b0), .a(1'b0), .b(1'b1), .e(1'b0), .d(1'b0), .c(1'b1), .dp(1'b0));
  _7_Segment_Display u_7_segment_display_4 (
    .g(1'b0), .f(1'b1), .a(1'b1), .b(1'b1), .e(1'b1), .d(1'b1), .c(1'b1), .dp(1'b0));
  _7_Segment_Display u_7_segment_display_5 (
    .g(1'b1), .f(1'b1), .a(1'b1), .b(1'b1), .e(1'b0), .d(1'b1), .c(1'b1), .dp(1'b0));
  _7_Segment_Display u_7_segment_display_6 (
    .g(1'b0), .f(1'b1), .a(1'b1), .b(1'b1), .e(1'b1), .d(1'b1), .c(1'b1), .dp(1'b0));
  _7_Segment_Display u_7_segment_display_7 (
    .g(1'b0), .f(1'b1), .a(1'b1), .b(1'b1), .e(1'b1), .d(1'b1), .c(1'b1), .dp(1'b0));
  _7_Segment_Display u_7_segment_display_8 (
    .g(1'b1), .f(1'b0), .a(1'b1), .b(1'b1), .e(1'b1), .d(1'b1), .c(1'b0), .dp(1'b0));
  _7_Segment_Display u_7_segment_display_9 (
    .g(1'b0), .f(1'b1), .a(1'b1), .b(1'b1), .e(1'b1), .d(1'b1), .c(1'b1), .dp(1'b0));
  _7_Segment_Display u_7_segment_display_10 (
    .g(1'b0), .f(1'b1), .a(1'b1), .b(1'b1), .e(1'b1), .d(1'b1), .c(1'b1), .dp(1'b0));

  // Notes on the sheet:
  //   曾舒立PB19000200
endmodule
