// Logisim project week2-3_曾舒立PB19000200.circ as structural Verilog: 1 circuit, main circuit main
module main (
  input  sel,
  input  a,
  input  b,
  output out
);

  wire and_1_out, and_2_out, not_1_out;

  not not_1 (not_1_out, sel);
  and and_1 (and_1_out, not_1_out, a);
  and and_2 (and_2_out, sel, b);
  or or_1 (out, and_1_out, and_2_out);

  // Notes on the sheet:
  //   曾舒立PB19000200
endmodule
