// Logisim project week2-4_曾舒立PB19000200.circ as structural Verilog: 2 circuits, main circuit mux21
module mux21 (
  input  sel,
  input  a,
  input  b,
  output out
);

  wire and_1_out, and_2_out, not_1_out;

  not not_1 (not_1_out, sel);
  and and_1 (and_1_out, not_1_out, a);
  and and_2 (and_2_out, sel, b);
  or or_1 (out, and_1_out, and_2_out);

  // Notes on the sheet:
  //   曾舒立PB19000200
endmodule

module mux41 (
  input  sel1,
  input  sel0,
  input  a,
  input  b,
  input  c,
  input  d,
  output out
);

  wire mux21_1_out, mux21_2_out;

  mux21 mux21_1 (.sel(sel0), .a(a), .b(b), .out(mux21_1_out));
  mux21 mux21_2 (.sel(sel0), .a(c), .b(d), .out(mux21_2_out));
  mux21 mux21_3 (.sel(sel1), .a(mux21_1_out), .b(mux21_2_out), .out(out));

  // Notes on the sheet:
  //   曾舒立PB19000200
endmodule
