// Logisim project week2-6_曾舒立PB19000200.circ as structural Verilog: 1 circuit, main circuit main
module main (
  input  a,
  input  b,
  input  c,
  output s1,
  output s2
);

  wire xor_1_out;

  xor xor_1 (xor_1_out, a, b);
  xor xor_2 (s1, xor_1_out, c);
  not not_1 (s2, s1);

  // Notes on the sheet:
  //   a,b,c中1的个数的奇偶检验，s1=~s2,奇数则s1=0,偶数则s1=1.
  //   曾舒立PB19000200
endmodule
