// Logisim project PB19000200-曾舒立-week3-1.circ as structural Verilog: 10 circuits, main circuit main
module main (
  input  R,
  input  S,
  output Q,
  output nQ
);

  nand nand_1 (Q, R, nQ);
  nand nand_2 (nQ, Q, S);

  // Notes on the sheet:
  //   曾舒立PB19000200
endmodule

module SR_NAND (
  input  R,
  input  S,
  output Q,
  output nQ
);

  nand nand_1 (Q, R, nQ);
  nand nand_2 (nQ, Q, S);

  // Notes on the sheet:
  //   曾舒立PB19000200
endmodule

module D_nand (
  input  in_1,
  input  in_2,
  output out_3,
  output out_4
);

  wire not_1_out, not_2_out, or_1_out, or_2_out;

  not not_1 (not_1_out, in_1);
  not not_2 (not_2_out, in_2);
  or or_1 (or_1_out, not_1_out, not_2_out);
  or or_2 (or_2_out, in_1, not_2_out);
  SR_NAND sr_nand_1 (.R(or_1_out), .S(or_2_out), .Q(out_3), .nQ(out_4));

  // Notes on the sheet:
  //   PB19000200 曾舒立
endmodule

module D_ff_synset (
  input  in_1,
  input  in_2,
  output out_3,
  output out_4
);

  wire clock_1_out, d_nand_1_out_3, not_1_out, or_1_out;

  Clock clock_1 (.out(clock_1_out));
  or or_1 (or_1_out, in_1, in_2);
  not not_1 (not_1_out, clock_1_out);
  D_nand d_nand_1 (.in_1(or_1_out), .in_2(not_1_out), .out_3(d_nand_1_out_3));  // open: out_4
  D_nand d_nand_2 (.in_1(d_nand_1_out_3), .in_2(clock_1_out), .out_3(out_3), .out_4(out_4));

  // Notes on the sheet:
  //   PB19000200 曾舒立
endmodule

module D_rst_nand (
  input  D,
  input  C,
  input  nRST,
  output out_4,
  output out_5
);

  wire and_1_out, not_1_out, not_2_out, not_3_out, or_1_out, or_2_out, or_3_out;

  not not_1 (not_1_out, D);
  not not_2 (not_2_out, C);
  or or_1 (or_1_out, not_1_out, not_2_out);
  or or_2 (or_2_out, D, not_2_out);
  not not_3 (not_3_out, nRST);
  or or_3 (or_3_out, or_1_out, not_3_out);
  and and_1 (and_1_out, or_2_out, nRST);
  SR_NAND sr_nand_1 (.R(or_3_out), .S(and_1_out), .Q(out_4), .nQ(out_5));

  // Notes on the sheet:
  //   PB19000200 曾舒立
endmodule

module D_ff_asynrst (
  input  D,
  input  clk,
  input  nrst,
  output out_4,
  output out_5
);

  wire d_rst_nand_1_out_4, not_1_out;

  not not_1 (not_1_out, clk);
  D_rst_nand d_rst_nand_1 (.D(D), .C(not_1_out), .nRST(nrst), .out_4(d_rst_nand_1_out_4));  // open: out_5
  D_rst_nand d_rst_nand_2 (.D(d_rst_nand_1_out_4), .C(clk), .nRST(nrst), .out_4(out_4), .out_5(out_5));

  // Notes on the sheet:
  //   PB19000200 曾舒立
endmodule

module _4bit_reg (
  input  [3:0] in_1,
  input  in_2,
  input  in_3,
  output [3:0] out_4
);

  D_ff_asynrst d_ff_asynrst_1 (.D(in_1[0]), .clk(in_2), .nrst(in_3), .out_4(out_4[0]));  // open: out_5
  D_ff_asynrst d_ff_asynrst_2 (.D(in_1[1]), .clk(in_2), .nrst(in_3), .out_4(out_4[1]));  // open: out_5
  D_ff_asynrst d_ff_asynrst_3 (.D(in_1[2]), .clk(in_2), .nrst(in_3), .out_4(out_4[2]));  // open: out_5
  D_ff_asynrst d_ff_asynrst_4 (.D(in_1[3]), .clk(in_2), .nrst(in_3), .out_4(out_4[3]));  // open: out_5

  // Notes on the sheet:
  //   PB19000200 曾舒立
endmodule

module _4_bit_count (
  input  in_1,
  output [3:0] out_2
);

  wire clock_1_out;
  wire [3:0] adder_1_out;

  Clock clock_1 (.out(clock_1_out));
  Adder #(.width(4)) adder_1 (.a(out_2), .b(4'b0001), .out(adder_1_out));  // open: cin, cout
  _4bit_reg u_4bit_reg_1 (.in_1(adder_1_out), .in_2(clock_1_out), .in_3(in_1), .out_4(out_2));

  // Notes on the sheet:
  //   PB19000200 曾舒立
endmodule

module _4_bit_1_minus (
  input  in_1,
  output [3:0] out_2
);

  wire and_1_out, clock_1_out;
  wire [3:0] and_2_out, n4bit_reg_1_out_4, subtractor_1_out;

  Subtractor #(.width(4)) subtractor_1 (.a(n4bit_reg_1_out_4), .b(4'b0001), .out(subtractor_1_out));  // open: bin, bout
  and and_1 (and_1_out, subtractor_1_out[0], subtractor_1_out[1], subtractor_1_out[2], subtractor_1_out[3]);
  and and_2 (and_2_out[0], and_1_out, 1'b0);
  and and_3 (and_2_out[1], and_1_out, 1'b1);
  and and_4 (and_2_out[2], and_1_out, 1'b1);
  and and_5 (and_2_out[3], and_1_out, 1'b0);
  Subtractor #(.width(4)) subtractor_2 (.a(subtractor_1_out), .b(and_2_out), .out(out_2));  // open: bin, bout
  Clock clock_1 (.out(clock_1_out));
  _4bit_reg u_4bit_reg_1 (.in_1(out_2), .in_2(clock_1_out), .in_3(in_1), .out_4(n4bit_reg_1_out_4));

  // Notes on the sheet:
  //   PB19000200 曾舒立
endmodule

module week3_5 (
  input  D,
  input  clk,
  input  RST,
  output out_4,
  output out_5
);

  wire d_rst_nand_1_out_4, not_1_out, not_2_out;

  not not_1 (not_1_out, clk);
  not not_2 (not_2_out, RST);
  D_rst_nand d_rst_nand_1 (.D(D), .C(not_1_out), .nRST(not_2_out), .out_4(d_rst_nand_1_out_4));  // open: out_5
  D_rst_nand d_rst_nand_2 (.D(d_rst_nand_1_out_4), .C(clk), .nRST(not_2_out), .out_4(out_4), .out_5(out_5));

  // Notes on the sheet:
  //   PB19000200 曾舒立
endmodule
