// Logisim project week8_2.circ as structural Verilog: 1 circuit, main circuit main
module main (
  input  CLK,
  input  SW,
  input  RST,
  output [3:0] out_4
);

  wire d_ff_1_q, d_ff_2_q, xor_1_out;
  wire [3:0] adder_1_out;

  D_Flip_Flop d_ff_1 (.clk(CLK), .D(SW), .Q(d_ff_1_q));  // open: Qn, preset, en, reset
  D_Flip_Flop d_ff_2 (.clk(CLK), .D(d_ff_1_q), .Q(d_ff_2_q));  // open: Qn, preset, en, reset
  Adder #(.width(4)) adder_1 (.a(4'b0001), .b(out_4), .out(adder_1_out), .cin(1'b0));  // open: cout
  xor xor_1 (xor_1_out, d_ff_2_q, d_ff_1_q);
  D_Flip_Flop d_ff_3 (.clk(xor_1_out), .D(adder_1_out[3]), .Q(out_4[3]), .reset(RST));  // open: Qn, preset, en
  D_Flip_Flop d_ff_4 (.clk(xor_1_out), .D(adder_1_out[2]), .Q(out_4[2]), .reset(RST));  // open: Qn, preset, en
  D_Flip_Flop d_ff_5 (.clk(xor_1_out), .D(adder_1_out[1]), .Q(out_4[1]), .reset(RST));  // open: Qn, preset, en
  D_Flip_Flop d_ff_6 (.clk(xor_1_out), .D(adder_1_out[0]), .Q(out_4[0]), .reset(RST));  // open: Qn, preset, en

  // Notes on the sheet:
  //   曾舒立PB19000200
endmodule
